# Fritzing sketch fritzing_diagram (saved by Fritzing 0.9.3b)

parts:
  Part1 = Arduino Uno (Rev3)
  PIR1 = PIR sensor

nets:
  N1: Part1.D2, PIR1.SIG
  5V: Part1.5V, PIR1.VDD
  GND: Part1.GND, PIR1.GND
